# Fritzing sketch schematic_project (saved by Fritzing 0.9.3b)

parts:
  Part1 = Arduino Nano (Rev3.0)
  S1 = Pushbutton [package="[THT]"]
  R1 = Rotary Potentiometer (Small) [maximum_resistance=100kΩ package=THT]
  Power_plug1 = Power plug
  J2 = male pin header, 3 pins [form="♂ (male)"]
  S2 = Pushbutton [package="[THT]"]
  Part2 = LCD1602-I2C

nets:
  GND: Part1.GND, S1.Pin_3, S1.Pin_4, Power_plug1.GND
  N1: Part1.D3, S1.Pin_2
  N2: Part1.D4, S2.Pin_2
  VIN: Part1.VIN, Power_plug1.VCC, J2.pin2
  N3: Part1.5V, R1.leg1
  N4: Part1.A7, R1.wiper
  N5: Part1.A5, Part2.SCL
  N6: Part1.A4, Part2.SDA
  N7: Part1.A2, J2.pin1

custom parts:
  LCD1602-I2C: A standard character display, usually with 2x16 characters. Comes in many colors with LCM1602 IIC attached.
